# Fritzing sketch Weather_Station (saved by Fritzing 0.9.3b)
breadboards: 1

parts:
  Part3 = Adafruit BME280
  SparkFun_ESP8266_Thing_-_Dev_Board2 = SparkFun ESP8266 Thing - Dev Board [part_number=WRL-13711]
  Part4 = Adafruit 1.54" Tri-Color eInk / ePaper Display with SRAM [part_number=3625]
  3_7v = LIPO-2000mAh [package=lipo-2000]

nets:
  VIN: Part3.VIN, SparkFun_ESP8266_Thing_-_Dev_Board2.VCC
  GND: Part3.GND, SparkFun_ESP8266_Thing_-_Dev_Board2.GND, Part4.GND, 3_7v.-
  N1: Part3.SCK/SCL, SparkFun_ESP8266_Thing_-_Dev_Board2.GPIO14, Part4.SCLK
  N2: Part3.SDI/SDA, SparkFun_ESP8266_Thing_-_Dev_Board2.GPIO2
  N3: SparkFun_ESP8266_Thing_-_Dev_Board2.RESET, Part4.RESET
  N4: SparkFun_ESP8266_Thing_-_Dev_Board2.USBVCC, Part4.VIN
  N5: SparkFun_ESP8266_Thing_-_Dev_Board2.GPIO5, Part4.DISPCS
  N6: SparkFun_ESP8266_Thing_-_Dev_Board2.GPIO0, Part4.DC
  N7: SparkFun_ESP8266_Thing_-_Dev_Board2.GPIO4, Part4.SRAMCS
  N8: SparkFun_ESP8266_Thing_-_Dev_Board2.GPIO13, Part4.MOSI
  N9: SparkFun_ESP8266_Thing_-_Dev_Board2.GPIO12, Part4.MISO
  N10: SparkFun_ESP8266_Thing_-_Dev_Board2.GPIO16, Part4.ENABLE
  N11: SparkFun_ESP8266_Thing_-_Dev_Board2.VIN, 3_7v.+

notes:
  DISPCS == ECS

custom parts:
  Adafruit BME280: Bosch has stepped up their game with their new BME280 sensor, an environmental sensor with temperature, barometric pressure and humidity! This sensor is great for all sorts of weather/environmental sensing and can even be used in both I2C and SPI! This precision sensor from Bosch is the best low-cost sensing solution for measuring humidity with ±3% accuracy, barometric pressure with ±1 hPa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
  SparkFun ESP8266 Thing - Dev Board: This is the SparkFun ESP8266 Thing Dev Board – a development board that has been solely designed around the ESP8266, with an integrated FTDI USB-to-Serial chip. The ESP8266 is a cost-effective, and very capable WiFi-enabled microcontroller. Like any microcontroller, it can be programmed to blink LEDs, trigger relays, monitor sensors, or automate coffee makers, and with an integrated WiFi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
  Adafruit 1.54" Tri-Color eInk / ePaper Display with SRAM: This small 1.54" tri-color display has 152x152 black and red ink pixels and a white-ish background. Using our Arduino library, you can create a 'frame buffer' with what pixels you want to have activated and then write that out to the display. We tossed a small SRAM chip on the back. This chip shares the SPI port the eInk display uses, so you only need one extra pin. And, no more frame-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
